// Logisim project Laboratorio2.circ as structural Verilog: 8 circuits, main circuit main
module main (
  input  in_1,
  input  in_2
);

  wire button_1_out, button_2_out, button_3_out, button_4_out, dotmatrix_1_p1, dotmatrix_1_p2;
  wire [6:0] Da, Dp, Ua, Up;

  Button button_1 (.out(button_1_out));
  Button button_2 (.out(button_2_out));
  Joystick joystick_1 ();  // open: x, y
  // DotMatrix #(.dotshape("circle"), .inputtype("select"), .matrixcols(16), .matrixrows(17)) dotmatrix_1: pin names not known; wires that end beside it: dotmatrix_1_p1, dotmatrix_1_p2, dotmatrix_1_p1, dotmatrix_1_p2
  ContadorUnitario contadorunitario_1 (
    .action(in_1), .push(button_1_out), .Reset(button_2_out), .Decenas(Da), .Unidades(Ua));
  _7_Segment_Display #(.decimalPoint("false")) u_7_segment_display_1 (
    .g(Da[6]), .f(Da[5]), .a(Da[0]), .b(Da[1]), .e(Da[4]), .d(Da[3]), .c(Da[2]));
  _7_Segment_Display #(.decimalPoint("false")) u_7_segment_display_2 (
    .g(Dp[6]), .f(Dp[5]), .a(Dp[0]), .b(Dp[1]), .e(Dp[4]), .d(Dp[3]), .c(Dp[2]));
  Button button_3 (.out(button_3_out));
  Button button_4 (.out(button_4_out));
  _7_Segment_Display #(.decimalPoint("false")) u_7_segment_display_3 (
    .g(Ua[6]), .f(Ua[5]), .a(Ua[0]), .b(Ua[1]), .e(Ua[4]), .d(Ua[3]), .c(Ua[2]));
  _7_Segment_Display #(.decimalPoint("false")) u_7_segment_display_4 (
    .g(Up[6]), .f(Up[5]), .a(Up[0]), .b(Up[1]), .e(Up[4]), .d(Up[3]), .c(Up[2]));
  ContadorUnitario contadorunitario_2 (
    .action(in_2), .push(button_3_out), .Reset(button_4_out), .Decenas(Dp), .Unidades(Up));

  // Notes on the sheet:
  //   "Catch a falling star"
  //   Estrellas Atrapadas
  //   Estrellas Pasadas
endmodule

module BCD7SEG (
  input  min,
  input  in_2,
  input  in_3,
  input  max,
  output a,
  output b,
  output c,
  output d,
  output e,
  output f,
  output g
);

  wire and_1_out, and_2_out, and_3_out, and_4_out, and_5_out, and_6_out, and_7_out, and_8_out, and_9_out,
       and_10_out, and_11_out, and_12_out, and_13_out, and_14_out, and_15_out, and_16_out, and_17_out,
       and_18_out, and_19_out, and_20_out, and_21_out, and_22_out, and_23_out, and_24_out, and_25_out,
       not_1_out, not_2_out, not_3_out, not_4_out;

  not not_1 (not_1_out, max);
  not not_2 (not_2_out, in_3);
  not not_3 (not_3_out, in_2);
  not not_4 (not_4_out, min);
  and and_1 (and_1_out, not_1_out, not_2_out, not_4_out);
  and and_2 (and_2_out, not_1_out, in_2);
  and and_3 (and_3_out, not_1_out, in_3, min);
  and and_4 (and_4_out, max, not_2_out, not_3_out);
  and and_5 (and_5_out, not_1_out, not_2_out);
  and and_6 (and_6_out, not_1_out, not_3_out, not_4_out);
  and and_7 (and_7_out, not_2_out, not_3_out);
  and and_8 (and_8_out, not_1_out, in_2, min);
  and and_9 (and_9_out, not_2_out, not_3_out);
  and and_10 (and_10_out, not_1_out, min);
  and and_11 (and_11_out, not_1_out, in_3);
  and and_12 (and_12_out, not_2_out, not_3_out, not_4_out);
  and and_13 (and_13_out, not_1_out, not_2_out, in_2);
  and and_14 (and_14_out, not_1_out, in_2, not_4_out);
  and and_15 (and_15_out, not_1_out, in_3, not_3_out, min);
  and and_16 (and_16_out, not_2_out, not_3_out, not_4_out);
  and and_17 (and_17_out, not_1_out, in_2, not_4_out);
  and and_18 (and_18_out, not_1_out, not_3_out, not_4_out);
  and and_19 (and_19_out, not_1_out, in_3, not_3_out);
  and and_20 (and_20_out, not_1_out, in_3, not_4_out);
  and and_21 (and_21_out, max, not_2_out, not_3_out);
  and and_22 (and_22_out, not_1_out, not_2_out, in_2);
  and and_23 (and_23_out, not_1_out, in_3, not_3_out);
  and and_24 (and_24_out, not_1_out, in_3, not_4_out);
  and and_25 (and_25_out, max, not_2_out, not_3_out);
  or or_1 (a, and_1_out, and_2_out, and_3_out, and_4_out);
  or or_2 (b, and_5_out, and_6_out, and_7_out, and_8_out);
  or or_3 (c, and_9_out, and_10_out, and_11_out);
  or or_4 (d, and_12_out, and_13_out, and_14_out, and_15_out);
  or or_5 (e, and_16_out, and_17_out);
  or or_6 (f, and_18_out, and_19_out, and_20_out, and_21_out);
  or or_7 (g, and_22_out, and_23_out, and_24_out, and_25_out);
endmodule

module BCD7SEGx2 (
  input  [6:0] inBCDx2,
  output Dg,
  output Df,
  output De,
  output Dd,
  output Dc,
  output Db,
  output Da,
  output Ug,
  output Uf,
  output Ue,
  output Ud,
  output Uc,
  output Ub,
  output Ua
);

  wire [6:0] divider_1_out, divider_1_rem;

  Divider #(.width(7)) divider_1 (
    .a(inBCDx2), .b(7'b0001010), .out(divider_1_out), .rem(divider_1_rem));  // open: upper
  // Probe on divider_1_rem
  // Probe on divider_1_out
  _7_Segment_Display u_7_segment_display_1 (.g(Dg), .f(Df), .a(Da), .b(Db), .e(De), .d(Dd), .c(Dc));  // open: dp
  _7_Segment_Display u_7_segment_display_2 (.g(Ug), .f(Uf), .a(Ua), .b(Ub), .e(Ue), .d(Ud), .c(Uc));  // open: dp
  BCD7SEG Decenas (
    .min(divider_1_out[0]), .in_2(divider_1_out[1]), .in_3(divider_1_out[2]), .max(divider_1_out[3]), .a(Da),
    .b(Db), .c(Dc), .d(Dd), .e(De), .f(Df), .g(Dg));
  BCD7SEG Unidades (
    .min(divider_1_rem[0]), .in_2(divider_1_rem[1]), .in_3(divider_1_rem[2]), .max(divider_1_rem[3]), .a(Ua),
    .b(Ub), .c(Uc), .d(Ud), .e(Ue), .f(Uf), .g(Ug));

  // Other names for the same wires on the sheet: a = Da; a1 = Ua; b = Db; b1 = Ub; c = Dc; c1 = Uc; d = Dd; d1 = Ud;
  //   e = De; e1 = Ue; f = Df; f1 = Uf; g = Dg; g1 = Ug
endmodule

module ContadorUnitario (
  input  action,
  input  push,
  input  Reset,
  output [6:0] Decenas,
  output [6:0] Unidades
);

  wire and_1_out, j_k_ff_1_qn, j_k_ff_2_qn, j_k_ff_3_qn, j_k_ff_4_qn, j_k_ff_5_qn, j_k_ff_6_qn, or_1_out;
  wire [6:0] j_k_ff_1_q;

  or or_1 (or_1_out, Reset, and_1_out);
  J_K_Flip_Flop j_k_ff_1 (
    .J(action), .K(action), .clk(push), .Q(j_k_ff_1_q[0]), .Qn(j_k_ff_1_qn), .reset(or_1_out));  // open: preset
  and and_1 (and_1_out, j_k_ff_1_q[6], j_k_ff_1_q[5], j_k_ff_1_q[2]);
  J_K_Flip_Flop j_k_ff_2 (
    .J(action), .K(action), .clk(j_k_ff_1_qn), .Q(j_k_ff_1_q[1]), .Qn(j_k_ff_2_qn), .reset(or_1_out));  // open: preset
  BCD7SEGx2 bcd7segx2_1 (
    .inBCDx2(j_k_ff_1_q), .Dg(Decenas[6]), .Df(Decenas[5]), .De(Decenas[4]), .Dd(Decenas[3]),
    .Dc(Decenas[2]), .Db(Decenas[1]), .Da(Decenas[0]), .Ug(Unidades[6]), .Uf(Unidades[5]), .Ue(Unidades[4]),
    .Ud(Unidades[3]), .Uc(Unidades[2]), .Ub(Unidades[1]), .Ua(Unidades[0]));
  J_K_Flip_Flop j_k_ff_3 (
    .J(action), .K(action), .clk(j_k_ff_2_qn), .Q(j_k_ff_1_q[2]), .Qn(j_k_ff_3_qn), .reset(or_1_out));  // open: preset
  J_K_Flip_Flop j_k_ff_4 (
    .J(action), .K(action), .clk(j_k_ff_3_qn), .Q(j_k_ff_1_q[3]), .Qn(j_k_ff_4_qn), .reset(or_1_out));  // open: preset
  J_K_Flip_Flop j_k_ff_5 (
    .J(action), .K(action), .clk(j_k_ff_4_qn), .Q(j_k_ff_1_q[4]), .Qn(j_k_ff_5_qn), .reset(or_1_out));  // open: preset
  J_K_Flip_Flop j_k_ff_6 (
    .J(action), .K(action), .clk(j_k_ff_5_qn), .Q(j_k_ff_1_q[5]), .Qn(j_k_ff_6_qn), .reset(or_1_out));  // open: preset
  J_K_Flip_Flop j_k_ff_7 (
    .J(action), .K(action), .clk(j_k_ff_6_qn), .Q(j_k_ff_1_q[6]), .reset(or_1_out));  // open: Qn, preset
  _7_Segment_Display u_7_segment_display_1 (
    .g(Decenas[6]), .f(Decenas[5]), .a(Decenas[0]), .b(Decenas[1]), .e(Decenas[4]), .d(Decenas[3]),
    .c(Decenas[2]));  // open: dp
  _7_Segment_Display u_7_segment_display_2 (
    .g(Unidades[6]), .f(Unidades[5]), .a(Unidades[0]), .b(Unidades[1]), .e(Unidades[4]), .d(Unidades[3]),
    .c(Unidades[2]));  // open: dp

  // Other names for the same wires on the sheet: a = Decenas[0]; b = Decenas[1]; c = Decenas[2]; d = Decenas[3];
  //   e = Decenas[4]; f = Decenas[5]; g = Decenas[6]; a1 = Unidades[0]; b1 = Unidades[1]; c1 = Unidades[2];
  //   d1 = Unidades[3]; e1 = Unidades[4]; f1 = Unidades[5]; g1 = Unidades[6]
endmodule

module ControlMove (
  input  [15:0] in_1,
  input  Reset,
  input  in_3,
  input  in_4,
  output [1:0] out_5
);

  wire and_1_out, clock_1_out, comparator_1_eq, comparator_2_eq, not_1_out, not_2_out, t_ff_1_q, t_ff_2_q;
  wire [3:0] counter_1_q, counter_2_q;
  wire [6:0] Da, Dp, Ua, Up;
  wire [15:0] catchstar_1_outx16, ctrl, demultiplexer_1_out0, demultiplexer_1_out1, demultiplexer_1_out2,
       demultiplexer_1_out3, demultiplexer_1_out4, demultiplexer_1_out5, demultiplexer_1_out6,
       demultiplexer_1_out7, demultiplexer_1_out8, demultiplexer_1_out9, demultiplexer_1_out10,
       demultiplexer_1_out11, demultiplexer_1_out12, demultiplexer_1_out13, demultiplexer_1_out14, limite,
       registre_1_outx16;

  Comparator #(.width(16)) comparator_1 (.a({16{1'b0}}), .b(limite), .eq(comparator_1_eq));  // open: gt, lt
  Clock clock_1 (.out(clock_1_out));
  Comparator #(.width(16)) comparator_2 (.a(ctrl), .b(limite), .eq(comparator_2_eq));  // open: gt, lt
  not not_1 (not_1_out, comparator_2_eq);
  not not_2 (not_2_out, comparator_1_eq);
  T_Flip_Flop t_ff_1 (.T(1'b1), .clk(clock_1_out), .Q(t_ff_1_q));  // open: Qn, reset, preset
  and and_1 (and_1_out, not_1_out, not_2_out);
  T_Flip_Flop t_ff_2 (.T(1'b1), .clk(t_ff_1_q), .Q(t_ff_2_q));  // open: Qn, reset, preset
  // Probe on catchstar_1_outx16
  catchStar catchstar_1 (.inx16(ctrl), .comparador(counter_1_q), .outx16(catchstar_1_outx16));
  Registre registre_1 (.outx16(registre_1_outx16), .inx16Disable(catchstar_1_outx16), .inx16Enable(in_1), .Rst(Reset));
  Counter #(.max('hf), .width(4)) counter_1 (.Q(counter_1_q), .clk(t_ff_2_q));  // open: load, D, count, carry, up, clr
  ContadorUnitario contadorunitario_1 (
    .action(in_3), .push(comparator_2_eq), .Reset(Reset), .Decenas(Da), .Unidades(Ua));
  Demultiplexer #(.enable("false"), .select(4), .width(16)) demultiplexer_1 (
    .out0(demultiplexer_1_out0), .out1(demultiplexer_1_out1), .out2(demultiplexer_1_out2),
    .out3(demultiplexer_1_out3), .out4(demultiplexer_1_out4), .out5(demultiplexer_1_out5),
    .out6(demultiplexer_1_out6), .out7(demultiplexer_1_out7), .out8(demultiplexer_1_out8),
    .out9(demultiplexer_1_out9), .out10(demultiplexer_1_out10), .out11(demultiplexer_1_out11),
    .out12(demultiplexer_1_out12), .out13(demultiplexer_1_out13), .out14(demultiplexer_1_out14),
    .out15(limite), .in(registre_1_outx16), .sel(counter_1_q));
  Counter #(.max('hf), .width(4)) counter_2 (
    .clr(Reset), .up(out_5[1]), .count(out_5[0]), .clk(clock_1_out), .Q(counter_2_q));  // open: load, D, carry
  ContadorUnitario contadorunitario_2 (.action(in_4), .push(and_1_out), .Reset(Reset), .Decenas(Dp), .Unidades(Up));
  DotMatrix #(.inputtype("row"), .matrixcols(16), .matrixrows(17)) dotmatrix_1 (
    .row0(demultiplexer_1_out0), .row1(demultiplexer_1_out1), .row2(demultiplexer_1_out2),
    .row3(demultiplexer_1_out3), .row4(demultiplexer_1_out4), .row5(demultiplexer_1_out5),
    .row6(demultiplexer_1_out6), .row7(demultiplexer_1_out7), .row8(demultiplexer_1_out8),
    .row9(demultiplexer_1_out9), .row10(demultiplexer_1_out10), .row11(demultiplexer_1_out11),
    .row12(demultiplexer_1_out12), .row13(demultiplexer_1_out13), .row14(demultiplexer_1_out14),
    .row15(limite), .row16(ctrl));
  // Probe on limite
  // Probe on counter_2_q
  Joystick #(.bits(2)) joystick_1 (.x(out_5));  // open: y
  Decoder #(.select(4)) decoder_1 (
    .out0(ctrl[15]), .out1(ctrl[14]), .out2(ctrl[13]), .out3(ctrl[12]), .out4(ctrl[11]), .out5(ctrl[10]),
    .out6(ctrl[9]), .out7(ctrl[8]), .out8(ctrl[7]), .out9(ctrl[6]), .out10(ctrl[5]), .out11(ctrl[4]),
    .out12(ctrl[3]), .out13(ctrl[2]), .out14(ctrl[1]), .out15(ctrl[0]), .sel(counter_2_q));  // open: en
  _7_Segment_Display #(.decimalPoint("false")) u_7_segment_display_1 (
    .g(Da[6]), .f(Da[5]), .a(Da[0]), .b(Da[1]), .e(Da[4]), .d(Da[3]), .c(Da[2]));
  _7_Segment_Display #(.decimalPoint("false")) u_7_segment_display_2 (
    .g(Dp[6]), .f(Dp[5]), .a(Dp[0]), .b(Dp[1]), .e(Dp[4]), .d(Dp[3]), .c(Dp[2]));
  // Probe on ctrl
  _7_Segment_Display #(.decimalPoint("false")) u_7_segment_display_3 (
    .g(Ua[6]), .f(Ua[5]), .a(Ua[0]), .b(Ua[1]), .e(Ua[4]), .d(Ua[3]), .c(Ua[2]));
  _7_Segment_Display #(.decimalPoint("false")) u_7_segment_display_4 (
    .g(Up[6]), .f(Up[5]), .a(Up[0]), .b(Up[1]), .e(Up[4]), .d(Up[3]), .c(Up[2]));

  // Other names for the same wires on the sheet: Action[1:0] = out_5; R = Reset

  // Notes on the sheet:
  //   Estrellas Atrapadas
endmodule

module ControlMoveY (
  input  Rst,
  output [15:0] out_2,
  output [15:0] out_3,
  output [15:0] out_4,
  output [15:0] out_5,
  output [15:0] out_6,
  output [15:0] out_7,
  output [15:0] out_8,
  output [15:0] out_9,
  output [15:0] out_10,
  output [15:0] out_11,
  output [15:0] out_12,
  output [15:0] out_13,
  output [15:0] out_14,
  output [15:0] out_15,
  output [15:0] out_16,
  output [15:0] out_17
);

  // Registre registre_1: pin names not known; wires that end beside it: Rst, Rst, out_2
  // Registre registre_2: pin names not known; wires that end beside it: Rst, Rst, out_3
  // Registre registre_3: pin names not known; wires that end beside it: Rst, Rst, out_4
  // Registre registre_4: pin names not known; wires that end beside it: Rst, Rst, out_5
  // Registre registre_5: pin names not known; wires that end beside it: Rst, Rst, out_6
  // Registre registre_6: pin names not known; wires that end beside it: Rst, Rst, out_7
  // Registre registre_7: pin names not known; wires that end beside it: Rst, Rst, out_8
  // Registre registre_8: pin names not known; wires that end beside it: Rst, Rst, out_9
  // Registre registre_9: pin names not known; wires that end beside it: Rst, Rst, out_10
  // Registre registre_10: pin names not known; wires that end beside it: Rst, Rst, out_11
  // Registre registre_11: pin names not known; wires that end beside it: Rst, Rst, out_12
  // Registre registre_12: pin names not known; wires that end beside it: Rst, Rst, out_13
  // Registre registre_13: pin names not known; wires that end beside it: Rst, Rst, out_14
  // Registre registre_14: pin names not known; wires that end beside it: Rst, Rst, out_15
  // Registre registre_15: pin names not known; wires that end beside it: Rst, Rst, out_16
  // Registre registre_16: pin names not known; wires that end beside it: Rst, out_17
endmodule

module Registre (
  input  [15:0] inx16Enable,
  input  Rst,
  input  [15:0] inx16Disable,
  output [15:0] outx16
);

  wire clock_1_out;

  Clock clock_1 (.out(clock_1_out));
  J_K_Flip_Flop j_k_ff_1 (
    .J(inx16Enable[0]), .clk(clock_1_out), .K(inx16Disable[0]), .Q(outx16[0]), .reset(Rst));  // open: Qn, preset
  J_K_Flip_Flop j_k_ff_2 (
    .J(inx16Enable[1]), .clk(clock_1_out), .K(inx16Disable[1]), .Q(outx16[1]), .reset(Rst));  // open: Qn, preset
  J_K_Flip_Flop j_k_ff_3 (
    .J(inx16Enable[2]), .clk(clock_1_out), .K(inx16Disable[2]), .Q(outx16[2]), .reset(Rst));  // open: Qn, preset
  J_K_Flip_Flop j_k_ff_4 (
    .J(inx16Enable[3]), .clk(clock_1_out), .K(inx16Disable[3]), .Q(outx16[3]), .reset(Rst));  // open: Qn, preset
  J_K_Flip_Flop j_k_ff_5 (
    .J(inx16Enable[4]), .clk(clock_1_out), .K(inx16Disable[4]), .Q(outx16[4]), .reset(Rst));  // open: Qn, preset
  J_K_Flip_Flop j_k_ff_6 (
    .J(inx16Enable[5]), .clk(clock_1_out), .K(inx16Disable[5]), .Q(outx16[5]), .reset(Rst));  // open: Qn, preset
  J_K_Flip_Flop j_k_ff_7 (
    .J(inx16Enable[6]), .clk(clock_1_out), .K(inx16Disable[6]), .Q(outx16[6]), .reset(Rst));  // open: Qn, preset
  J_K_Flip_Flop j_k_ff_8 (
    .J(inx16Enable[7]), .clk(clock_1_out), .K(inx16Disable[7]), .Q(outx16[7]), .reset(Rst));  // open: Qn, preset
  J_K_Flip_Flop j_k_ff_9 (
    .J(inx16Enable[8]), .clk(clock_1_out), .K(inx16Disable[8]), .Q(outx16[8]), .reset(Rst));  // open: Qn, preset
  J_K_Flip_Flop j_k_ff_10 (
    .J(inx16Enable[9]), .clk(clock_1_out), .K(inx16Disable[9]), .Q(outx16[9]), .reset(Rst));  // open: Qn, preset
  J_K_Flip_Flop j_k_ff_11 (
    .J(inx16Enable[10]), .clk(clock_1_out), .K(inx16Disable[10]), .Q(outx16[10]), .reset(Rst));  // open: Qn, preset
  J_K_Flip_Flop j_k_ff_12 (
    .J(inx16Enable[11]), .clk(clock_1_out), .K(inx16Disable[11]), .Q(outx16[11]), .reset(Rst));  // open: Qn, preset
  J_K_Flip_Flop j_k_ff_13 (
    .J(inx16Enable[12]), .clk(clock_1_out), .K(inx16Disable[12]), .Q(outx16[12]), .reset(Rst));  // open: Qn, preset
  J_K_Flip_Flop j_k_ff_14 (
    .J(inx16Enable[13]), .clk(clock_1_out), .K(inx16Disable[13]), .Q(outx16[13]), .reset(Rst));  // open: Qn, preset
  J_K_Flip_Flop j_k_ff_15 (
    .J(inx16Enable[14]), .clk(clock_1_out), .K(inx16Disable[14]), .Q(outx16[14]), .reset(Rst));  // open: Qn, preset
  J_K_Flip_Flop j_k_ff_16 (
    .J(inx16Enable[15]), .clk(clock_1_out), .K(inx16Disable[15]), .Q(outx16[15]), .reset(Rst));  // open: Qn, preset

  // Notes on the sheet:
  //   Bits horizontales
endmodule

module catchStar (
  input  [15:0] inx16,
  input  [3:0] comparador,
  output [15:0] outx16
);

  wire r;

  Comparator #(.width(4)) comparator_1 (.a(comparador), .b(4'b1111), .eq(r));  // open: gt, lt
  and and_1 (outx16[8], inx16[8], r);
  and and_2 (outx16[9], inx16[9], r);
  and and_3 (outx16[10], inx16[10], r);
  and and_4 (outx16[11], inx16[11], r);
  and and_5 (outx16[12], inx16[12], r);
  and and_6 (outx16[13], inx16[13], r);
  and and_7 (outx16[14], inx16[14], r);
  and and_8 (outx16[15], inx16[15], r);
  and and_9 (outx16[0], inx16[0], r);
  and and_10 (outx16[1], inx16[1], r);
  and and_11 (outx16[2], inx16[2], r);
  and and_12 (outx16[3], inx16[3], r);
  and and_13 (outx16[4], inx16[4], r);
  and and_14 (outx16[5], inx16[5], r);
  and and_15 (outx16[6], inx16[6], r);
  and and_16 (outx16[7], inx16[7], r);
endmodule
